# Fritzing sketch TaschenEinbau (saved by Fritzing 0.9.3b)

parts:
  U1 = atmega328 [package=dip]
  VCC1 = Battery
  R1 = Resistor [tolerance=±5% resistance=1k package=THT]
  R2 = Resistor [tolerance=±5% resistance=1k package=THT]
  R3 = Resistor [tolerance=±5% resistance=1k package=THT]
  R4 = Resistor [tolerance=±5% resistance=1k package=THT]
  S1 = Pushbutton [package=THT]
  S2 = Pushbutton [package=THT]
  S3 = Pushbutton [package=THT]
  S4 = Pushbutton [package=THT]
  LED1 = LED - 5mm [color="Red (633nm)" package="5 mm [THT]"]
  R5 = Resistor [tolerance=±5% resistance=220 package=THT]  # not connected
  J1 = Piezo Speaker
  J2 = female pin header, 1 pin [form="♀ (female)"]  # not connected
  S5 = Taiway 100-SP-X-T1 SPDT Miniature Toggle Switch [part_number=100-SP-X-T1-0-0-B1-M1 package=THT]  # not connected

nets:
  N1: U1.D0_(RX), R4.Pin_0
  N2: U1.D2, R3.Pin_0
  N3: U1.VCC, VCC1.+, R3.Pin_1, R4.Pin_1
  N4: U1.GND#7, VCC1.-
  N5: U1.D6_(PWM), R1.Pin_0, S3.leg0
  N6: U1.D8, R2.Pin_0, S4.leg0
  N7: U1.D11_(PWM), J1.pin2
  N8: U1.D13, LED1.cathode
  N9: U1.AVCC, R2.Pin_1
  N10: S1.leg1, S2.leg1, S3.leg1, S4.leg1

notes:
  Arduino 2 Pin 4
  Arduino 4 Pin 6
  Arduino 6 Pin 12
  Arduino 8 Pin 14
  Arduino 11 Pin 17
