# Fritzing sketch TaschenEinbau04 (saved by Fritzing 0.9.3b)

parts:
  U1 = atmega328 [package=dip]
  R2 = Resistor [tolerance=±5% resistance=1k package=THT]
  R3 = Resistor [tolerance=±5% resistance=1k package=THT]
  R4 = Resistor [tolerance=±5% resistance=1k package=THT]
  J1 = Piezo Speaker
  S5 = Taiway 100-SP-X-T1 SPDT Miniature Toggle Switch [part_number=100-SP-X-T1-0-0-B1-M1 package=THT]
  S6 = Taiway 100-SP-X-T1 SPDT Miniature Toggle Switch [part_number=100-SP-X-T1-0-0-B1-M1 package=THT]  # not connected
  S7 = Taiway 100-SP-X-T1 SPDT Miniature Toggle Switch [part_number=100-SP-X-T1-0-0-B1-M1 package=THT]
  S8 = Taiway 100-SP-X-T1 SPDT Miniature Toggle Switch [part_number=100-SP-X-T1-0-0-B1-M1 package=THT]
  S9 = Taiway 100-SP-X-T1 SPDT Miniature Toggle Switch [part_number=100-SP-X-T1-0-0-B1-M1 package=THT]  # not connected
  VCC1 = 4 x AAA Battery Mount

nets:
  N1: U1.D2, R3.Pin_1, S7.L1
  N2: U1.GND, VCC1.-
  N3: U1.D5_(PWM), R4.Pin_0, S8.L1
  N4: U1.D7, R2.Pin_0, S5.L2
  N5: U1.D11_(PWM), J1.pin2
  N6: U1.AVCC, R2.Pin_1, R3.Pin_0
